// Logisim project symulacja c).circ as structural Verilog: 2 circuits, main circuit main
module main (
  input  reset__CLR,
  input  S1,
  input  RIN,
  input  D,
  input  C,
  input  B,
  input  A
);

  wire clock_1_out, n74194_1_qa, n74194_1_qb, n74194_1_qc, n74194_1_qd, not_1_out;

  Clock clock_1 (.out(clock_1_out));
  _74194 u_74194_1 (
    .S0(1'b0), .S1(S1), .SR(RIN), .CLK(clock_1_out), .CLR(reset__CLR), .SL(not_1_out), .A(A), .B(B), .C(C),
    .D(D), .QA(n74194_1_qa), .QB(n74194_1_qb), .QC(n74194_1_qc), .QD(n74194_1_qd));
  not not_1 (not_1_out, n74194_1_qa);
  LED led_1 (.in(n74194_1_qd));
  LED led_2 (.in(n74194_1_qc));
  LED led_3 (.in(n74194_1_qb));
  LED led_4 (.in(n74194_1_qa));

  // Notes on the sheet:
  //   S0
  //   LIN
  //   zegar
  //   QD
  //   QC
  //   QB
  //   QA
endmodule

module _74194 (
  input  A,
  input  B,
  input  C,
  input  D,
  input  S0,
  input  S1,
  input  SR,
  input  SL,
  input  CLK,
  input  CLR,
  output QA,
  output QB,
  output QC,
  output QD
);

  wire and_1_out, and_2_out, and_3_out, and_4_out, and_5_out, and_6_out, and_7_out, and_8_out, and_9_out,
       and_10_out, and_11_out, and_12_out, and_13_out, nor_1_out, nor_2_out, nor_3_out, nor_4_out, nor_5_out,
       nor_6_out, not_1_out, not_2_out, not_3_out, not_4_out, not_5_out, not_6_out, not_7_out, not_8_out;

  not not_1 (not_1_out, S0);
  not not_2 (not_2_out, S1);
  not not_3 (not_3_out, CLK);
  not not_4 (not_4_out, CLR);
  nor nor_1 (nor_1_out, not_1_out, not_2_out);
  and and_1 (and_1_out, not_1_out, not_2_out);
  and and_2 (and_2_out, nor_1_out, A);
  and and_3 (and_3_out, SR, not_2_out);
  nor nor_2 (nor_2_out, and_3_out, and_2_out, and_4_out);
  nor nor_3 (nor_3_out, and_1_out, not_3_out);
  and and_4 (and_4_out, not_1_out, QB);
  S_R_Flip_Flop s_r_ff_1 (
    .S(not_5_out), .clk(nor_3_out), .R(nor_2_out), .Q(QA), .reset(not_4_out));  // open: Qn, preset, en
  not not_5 (not_5_out, nor_2_out);
  and and_5 (and_5_out, QA, not_2_out);
  and and_6 (and_6_out, nor_1_out, B);
  and and_7 (and_7_out, not_1_out, QC);
  nor nor_4 (nor_4_out, and_5_out, and_6_out, and_7_out);
  not not_6 (not_6_out, nor_4_out);
  S_R_Flip_Flop s_r_ff_2 (
    .S(not_6_out), .clk(nor_3_out), .R(nor_4_out), .Q(QB), .reset(not_4_out));  // open: Qn, preset, en
  and and_8 (and_8_out, nor_1_out, C);
  and and_9 (and_9_out, QB, not_2_out);
  nor nor_5 (nor_5_out, and_9_out, and_8_out, and_10_out);
  and and_10 (and_10_out, not_1_out, QD);
  S_R_Flip_Flop s_r_ff_3 (
    .S(not_7_out), .clk(nor_3_out), .R(nor_5_out), .Q(QC), .reset(not_4_out));  // open: Qn, preset, en
  not not_7 (not_7_out, nor_5_out);
  and and_11 (and_11_out, QC, not_2_out);
  and and_12 (and_12_out, not_1_out, SL);
  and and_13 (and_13_out, nor_1_out, D);
  nor nor_6 (nor_6_out, and_11_out, and_13_out, and_12_out);
  not not_8 (not_8_out, nor_6_out);
  S_R_Flip_Flop s_r_ff_4 (
    .S(not_8_out), .clk(nor_3_out), .R(nor_6_out), .Q(QD), .reset(not_4_out));  // open: Qn, preset, en
endmodule
