// Logisim project z2.circ as structural Verilog: 5 circuits, main circuit 74151 (MUX)
module _74151__MUX (
  input  G,
  input  D0,
  input  D1,
  input  D2,
  input  D3,
  input  D4,
  input  D5,
  input  D6,
  input  D7,
  input  A,
  input  B,
  input  C,
  output Y,
  output W
);

  wire and_1_out, and_2_out, and_3_out, and_4_out, and_5_out, and_6_out, and_7_out, and_8_out, not_1_out,
       not_2_out, not_3_out, not_4_out, not_5_out, not_6_out, not_7_out;

  not not_1 (not_1_out, G);
  not not_2 (not_2_out, A);
  not not_3 (not_3_out, B);
  not not_4 (not_4_out, C);
  not not_5 (not_5_out, not_2_out);
  not not_6 (not_6_out, not_3_out);
  not not_7 (not_7_out, not_4_out);
  and and_1 (and_1_out, D0, not_2_out, not_3_out, not_4_out, not_1_out);
  and and_2 (and_2_out, D1, not_5_out, not_3_out, not_4_out, not_1_out);
  and and_3 (and_3_out, D2, not_6_out, not_2_out, not_4_out, not_1_out);
  and and_4 (and_4_out, D3, not_5_out, not_6_out, not_4_out, not_1_out);
  and and_5 (and_5_out, D4, not_7_out, not_2_out, not_3_out, not_1_out);
  and and_6 (and_6_out, D5, not_5_out, not_3_out, not_7_out, not_1_out);
  and and_7 (and_7_out, D6, not_2_out, not_6_out, not_7_out, not_1_out);
  and and_8 (and_8_out, D7, not_5_out, not_6_out, not_7_out, not_1_out);
  not not_8 (Y, W);
  nor nor_1 (W, and_1_out, and_2_out, and_3_out, and_4_out, and_5_out, and_6_out, and_7_out, and_8_out);
endmodule

module Funkcja_a (
  input  a,
  input  b,
  input  c,
  input  d
);

  wire n74151_mux_1_w, n74151_mux_1_y, nand_1_out, nand_2_out, nand_3_out, not_1_out, not_2_out, not_3_out,
       not_4_out;

  LED led_1 (.in(n74151_mux_1_w));
  _74151__MUX u_74151_mux_1 (
    .G(d), .D0(1'b1), .D1(1'b1), .D2(1'b1), .D3(1'b1), .D4(1'b1), .D5(1'b0), .D6(1'b0), .D7(1'b0), .A(a),
    .B(b), .C(c), .Y(n74151_mux_1_y), .W(n74151_mux_1_w));
  LED led_2 (.in(n74151_mux_1_y));
  LED led_3 (.in(nand_3_out));
  not not_1 (not_1_out, a);
  not not_2 (not_2_out, b);
  not not_3 (not_3_out, c);
  not not_4 (not_4_out, d);
  nand nand_1 (nand_1_out, not_1_out, not_2_out, not_4_out);
  nand nand_2 (nand_2_out, not_3_out, not_4_out);
  nand nand_3 (nand_3_out, nand_1_out, nand_2_out);

  // Notes on the sheet:
  //   Funkcja a)
  //   MUX output
  //   A
  //   B
  //   C
  //   NAND output
  //   D
  //   ~A,~B,~D
  //   ~C,~D
endmodule

module Funkcja_b (
  input  A,
  input  B,
  input  C
);

  wire n74151_mux_1_w, n74151_mux_1_y, nand_1_out, nand_2_out, nand_3_out, nand_4_out, not_1_out, not_2_out,
       not_3_out;

  LED led_1 (.in(n74151_mux_1_w));
  _74151__MUX u_74151_mux_1 (
    .G(1'b0), .D0(1'b1), .D1(1'b1), .D2(1'b1), .D3(1'b0), .D4(1'b0), .D5(1'b1), .D6(1'b1), .D7(1'b1), .A(A),
    .B(B), .C(C), .Y(n74151_mux_1_y), .W(n74151_mux_1_w));
  LED led_2 (.in(n74151_mux_1_y));
  LED led_3 (.in(nand_4_out));
  not not_1 (not_1_out, A);
  not not_2 (not_2_out, B);
  not not_3 (not_3_out, C);
  nand nand_1 (nand_1_out, not_3_out, not_1_out);
  nand nand_2 (nand_2_out, A, not_2_out);
  nand nand_3 (nand_3_out, B, C);
  nand nand_4 (nand_4_out, nand_1_out, nand_2_out, nand_3_out);

  // Notes on the sheet:
  //   Funkcja b)
  //   MUX output
  //   NAND output
  //   ~A,~C
  //   A,~B
  //   C,B
endmodule

module zamiany_AND_OR_na_NAND (
  input  A,
  input  A_2,
  input  B,
  input  B_2,
  input  C,
  input  C_2,
  input  D,
  input  D_2,
  input  A_3,
  input  A_4,
  input  B_3,
  input  B_4,
  input  C_3,
  input  C_4
);

  wire and_1_out, and_2_out, and_3_out, and_4_out, and_5_out, nand_1_out, nand_2_out, nand_3_out, nand_4_out,
       nand_5_out, nand_6_out, nand_7_out, not_1_out, not_2_out, not_3_out, not_4_out, not_5_out, not_6_out,
       not_7_out, not_8_out, not_9_out, not_10_out, not_11_out, not_12_out, not_13_out, not_14_out, or_1_out,
       or_2_out;

  not not_1 (not_1_out, A);
  not not_2 (not_2_out, B);
  not not_3 (not_3_out, C);
  not not_4 (not_4_out, D);
  not not_5 (not_5_out, A_4);
  not not_6 (not_6_out, B_4);
  not not_7 (not_7_out, C_4);
  and and_1 (and_1_out, not_1_out, not_2_out, not_4_out);
  and and_2 (and_2_out, not_3_out, not_4_out);
  and and_3 (and_3_out, not_7_out, not_5_out);
  and and_4 (and_4_out, A_4, not_6_out);
  and and_5 (and_5_out, B_4, C_4);
  or or_1 (or_1_out, and_1_out, and_2_out);
  LED led_1 (.in(or_1_out));
  LED led_2 (.in(or_2_out));
  or or_2 (or_2_out, and_3_out, and_4_out, and_5_out);
  not not_8 (not_8_out, A_3);
  not not_9 (not_9_out, B_3);
  not not_10 (not_10_out, C_3);
  not not_11 (not_11_out, A_2);
  not not_12 (not_12_out, B_2);
  not not_13 (not_13_out, C_2);
  not not_14 (not_14_out, D_2);
  nand nand_1 (nand_1_out, not_11_out, not_12_out, not_14_out);
  nand nand_2 (nand_2_out, not_13_out, not_14_out);
  nand nand_3 (nand_3_out, not_10_out, not_8_out);
  nand nand_4 (nand_4_out, A_3, not_9_out);
  nand nand_5 (nand_5_out, B_3, C_3);
  nand nand_6 (nand_6_out, nand_1_out, nand_2_out);
  LED led_3 (.in(nand_6_out));
  LED led_4 (.in(nand_7_out));
  nand nand_7 (nand_7_out, nand_3_out, nand_4_out, nand_5_out);

  // Notes on the sheet:
  //   Funkcja a)
  //   Funkcja b)
  //   ~A,~B,~D
  //   ~C,~D
  //   ~A,~C
  //   A,~B
  //   C,B
  //   =
  //   =
  //   ~A,~B,~D
  //   ~C,~D
  //   ~A,~C
  //   A,~B
  //   C,B
endmodule

module a__alternatywnie (
  input  C,
  input  A,
  input  B,
  input  D
);

  wire and_1_out, and_2_out, n74151_mux_1_w, n74151_mux_1_y, n74151_mux_2_w, n74151_mux_2_y, not_1_out,
       or_1_out;

  LED led_1 (.in(n74151_mux_1_w));
  _74151__MUX u_74151_mux_1 (
    .G(1'b0), .D0(1'b1), .D1(1'b1), .D2(1'b1), .D3(1'b1), .D4(1'b1), .D5(1'b0), .D6(1'b0), .D7(1'b0), .A(A),
    .B(B), .C(D), .Y(n74151_mux_1_y), .W(n74151_mux_1_w));
  LED led_2 (.in(or_1_out));
  or or_1 (or_1_out, and_1_out, and_2_out);
  and and_1 (and_1_out, n74151_mux_1_y, not_1_out);
  not not_1 (not_1_out, C);
  and and_2 (and_2_out, C, n74151_mux_2_y);
  LED led_3 (.in(n74151_mux_2_w));
  _74151__MUX u_74151_mux_2 (
    .G(1'b0), .D0(1'b0), .D1(1'b0), .D2(1'b0), .D3(1'b0), .D4(1'b0), .D5(1'b0), .D6(1'b0), .D7(1'b0), .A(A),
    .B(B), .C(D), .Y(n74151_mux_2_y), .W(n74151_mux_2_w));

  // Notes on the sheet:
  //   Funkcja a)
  //   alternatywnie
  //   tj. ignorując fakt,
  //   że D może być sygnałem
  //   zezwalającym
  //   MUX output
endmodule
