// Logisim project z3.circ as structural Verilog: 7 circuits, main circuit 74151 (MUX) (nadprogramowo)
module _74151__MUX___nadprogramowo (
  input  G,
  input  D0,
  input  D1,
  input  D2,
  input  D3,
  input  D4,
  input  D5,
  input  D6,
  input  D7,
  input  A,
  input  B,
  input  C,
  output Y,
  output W
);

  wire and_1_out, and_2_out, and_3_out, and_4_out, and_5_out, and_6_out, and_7_out, and_8_out, not_1_out,
       not_2_out, not_3_out, not_4_out, not_5_out, not_6_out, not_7_out;

  not not_1 (not_1_out, G);
  not not_2 (not_2_out, A);
  not not_3 (not_3_out, B);
  not not_4 (not_4_out, C);
  not not_5 (not_5_out, not_2_out);
  not not_6 (not_6_out, not_3_out);
  not not_7 (not_7_out, not_4_out);
  and and_1 (and_1_out, D0, not_2_out, not_3_out, not_4_out, not_1_out);
  and and_2 (and_2_out, D1, not_5_out, not_3_out, not_4_out, not_1_out);
  and and_3 (and_3_out, D2, not_6_out, not_2_out, not_4_out, not_1_out);
  and and_4 (and_4_out, D3, not_5_out, not_6_out, not_4_out, not_1_out);
  and and_5 (and_5_out, D4, not_7_out, not_2_out, not_3_out, not_1_out);
  and and_6 (and_6_out, D5, not_5_out, not_3_out, not_7_out, not_1_out);
  and and_7 (and_7_out, D6, not_2_out, not_6_out, not_7_out, not_1_out);
  and and_8 (and_8_out, D7, not_5_out, not_6_out, not_7_out, not_1_out);
  not not_8 (Y, W);
  nor nor_1 (W, and_1_out, and_2_out, and_3_out, and_4_out, and_5_out, and_6_out, and_7_out, and_8_out);
endmodule

module Funkcja_na_rozne_sposoby__nadprogramowo (
  input  A,
  input  B,
  input  C,
  input  D,
  output AND_OR_output,
  output NAND_output,
  output MUX_AND_OR_output,
  output _3x_MUX_output
);

  wire and_1_out, and_2_out, and_3_out, and_4_out, n74151_mux_nadprogramowo_1_y,
       n74151_mux_nadprogramowo_2_y, nand_2_out, nand_3_out, not_1_out, not_2_out, not_3_out, not_4_out,
       not_5_out, not_6_out, not_7_out, not_8_out, not_9_out;

  and and_1 (and_1_out, not_1_out, not_2_out, D);
  not not_1 (not_1_out, A);
  not not_2 (not_2_out, B);
  _74151__MUX___nadprogramowo u_74151_mux_nadprogramowo_1 (
    .G(1'b0), .D0(1'b1), .D1(1'b1), .D2(1'b1), .D3(1'b1), .D4(1'b0), .D5(1'b0), .D6(1'b0), .D7(1'b0), .A(A),
    .B(B), .C(C), .Y(n74151_mux_nadprogramowo_1_y));  // open: W
  LED led_1 (.in(AND_OR_output));
  or or_1 (AND_OR_output, and_1_out, and_2_out);
  and and_2 (and_2_out, not_4_out, not_3_out);
  not not_3 (not_3_out, D);
  not not_4 (not_4_out, C);
  LED led_2 (.in(NAND_output));
  nand nand_1 (NAND_output, nand_2_out, nand_3_out);
  nand nand_2 (nand_2_out, not_6_out, not_5_out, D);
  not not_5 (not_5_out, B);
  not not_6 (not_6_out, A);
  nand nand_3 (nand_3_out, not_7_out, not_8_out);
  not not_7 (not_7_out, D);
  not not_8 (not_8_out, C);
  _74151__MUX___nadprogramowo u_74151_mux_nadprogramowo_2 (
    .G(1'b0), .D0(1'b1), .D1(1'b0), .D2(1'b0), .D3(1'b0), .D4(1'b1), .D5(1'b0), .D6(1'b0), .D7(1'b0), .A(A),
    .B(B), .C(C), .Y(n74151_mux_nadprogramowo_2_y));  // open: W
  LED led_3 (.in(MUX_AND_OR_output));
  or or_2 (MUX_AND_OR_output, and_4_out, and_3_out);
  and and_3 (and_3_out, not_9_out, n74151_mux_nadprogramowo_1_y);
  and and_4 (and_4_out, n74151_mux_nadprogramowo_2_y, D);
  not not_9 (not_9_out, D);
  LED led_4 (.in(_3x_MUX_output));
  _74151__MUX___nadprogramowo u_74151_mux_nadprogramowo_3 (
    .G(1'b0), .D0(n74151_mux_nadprogramowo_1_y), .D1(n74151_mux_nadprogramowo_2_y), .D2(1'b0), .D3(1'b0),
    .D4(1'b0), .D5(1'b0), .D6(1'b0), .D7(1'b0), .A(D), .B(1'b0), .C(1'b0), .Y(_3x_MUX_output));  // open: W

  // Notes on the sheet:
  //   f(a,b,c,0)
  //   Przypadek 1.
  //   Przypadek 2.
  //   Przypadek 3.
  //   f(a,b,c,1)
  //   f(a,b,c,0)
  //   Przypadek 4.
endmodule

module oscyloskop___D_Flip_Flop (
  input  CLK,
  input  D,
  output Q,
  output Q_prime
);

  D_Flip_Flop d_ff_1 (.clk(CLK), .D(D), .Q(Q), .Qn(Q_prime), .preset(1'b0), .en(1'b1), .reset(1'b0));

  // Notes on the sheet:
  //   uziemione CLR i PRE
  //   ENABLE na stałe z wejściem 1
endmodule

module funkcja (
  input  A,
  input  B,
  input  C,
  input  D,
  output hazard_output,
  output no_hazard_output
);

  wire nand_1_out, nand_3_out, nand_4_out, nand_5_out, nand_7_out, not_1_out, not_2_out, not_3_out,
       not_4_out, not_5_out, not_6_out, not_7_out, not_8_out, not_9_out, not_10_out, not_11_out,
       oscyloskop_d_ff_1_q, oscyloskop_d_ff_1_q_prime, oscyloskop_d_ff_2_q, oscyloskop_d_ff_2_q_prime;

  not not_1 (not_1_out, A);
  not not_2 (not_2_out, B);
  not not_3 (not_3_out, C);
  not not_4 (not_4_out, D);
  not not_5 (not_5_out, A);
  not not_6 (not_6_out, B);
  not not_7 (not_7_out, C);
  not not_8 (not_8_out, D);
  not not_9 (not_9_out, A);
  not not_10 (not_10_out, B);
  not not_11 (not_11_out, C);
  nand nand_1 (nand_1_out, not_1_out, not_2_out, D);
  nand nand_2 (hazard_output, nand_1_out, nand_3_out);
  nand nand_3 (nand_3_out, not_3_out, not_4_out);
  nand nand_4 (nand_4_out, not_5_out, not_6_out, D);
  nand nand_5 (nand_5_out, not_7_out, not_8_out);
  nand nand_6 (no_hazard_output, nand_4_out, nand_5_out, nand_7_out);
  nand nand_7 (nand_7_out, not_9_out, not_10_out, not_11_out);
  LED LED1 (.in(hazard_output));
  LED LED1__no_hazard (.in(no_hazard_output));
  oscyloskop___D_Flip_Flop oscyloskop_d_ff_1 (
    .CLK(hazard_output), .D(oscyloskop_d_ff_1_q_prime), .Q(oscyloskop_d_ff_1_q),
    .Q_prime(oscyloskop_d_ff_1_q_prime));
  LED LED2 (.in(oscyloskop_d_ff_1_q));
  LED LED2__no_hazard (.in(oscyloskop_d_ff_2_q));
  oscyloskop___D_Flip_Flop oscyloskop_d_ff_2 (
    .CLK(no_hazard_output), .D(oscyloskop_d_ff_2_q_prime), .Q(oscyloskop_d_ff_2_q),
    .Q_prime(oscyloskop_d_ff_2_q_prime));

  // Notes on the sheet:
  //   Funkcja z hazardem
  //   Funkcja bez hazardu
  //   Instrukcja "oscyloskopu":
  //   1. Jeśli ani LED1 ani LED2 nie zmienią stanu, to nie wystąpił hazard
  //   2. Jeśli LED1 nie zmieni stanu*, a LED2 go zmieni, to znaczy, że wystąpił hazard statyczny
  //   3.Jeśli LED1 zmienił stan z 0 na 1, LED2 też zmieni swój stan, chyba że wystąpił hazard dynamiczny**
  //   4.Jeśli LED1 zmienił stan z 1 na 0, LED2 nie powinien zmienić swojego stanu, chyba że wystąpił hazard dynamiczny
  //   *Jeśli nie zauważymy zmiany stanu, zmiana nastąpiła, lecz była ułamkiem sekundy - niedostrzegalna dla nas
  //   **LED2 zmieni stan dwukrotnie przy hazardzie dynamicznym, stąd wrażenie, że stan się nie zmienił
endmodule

module _7474_jeden_przerzutnik__nadprogramowo (
  input  PRE,
  input  CLR,
  input  CLK,
  input  D,
  output Q,
  output Q_prime
);

  wire nand_1_out, nand_2_out, nand_3_out, nand_4_out;

  nand nand_1 (nand_1_out, PRE, nand_4_out, nand_2_out);
  nand nand_2 (nand_2_out, nand_1_out, CLR, CLK);
  nand nand_3 (nand_3_out, nand_2_out, CLK, nand_4_out);
  nand nand_4 (nand_4_out, nand_3_out, CLR, D);
  nand nand_5 (Q, PRE, nand_2_out, Q_prime);
  nand nand_6 (Q_prime, Q, nand_3_out, CLR);
endmodule

module funkcja_alternatywnie__nadprogramowo (
  input  CLR,
  input  PRE,
  input  A,
  input  B,
  input  C,
  input  D,
  input  CLR_2,
  input  PRE_2,
  output hazard_output,
  output no_hazard_output
);

  wire n7474_jeden_przerzutnik_nadprogramowo_1_q, n7474_jeden_przerzutnik_nadprogramowo_1_q_prime,
       n7474_jeden_przerzutnik_nadprogramowo_2_q, n7474_jeden_przerzutnik_nadprogramowo_2_q_prime,
       nand_1_out, nand_3_out, nand_4_out, nand_5_out, nand_7_out, not_1_out, not_2_out, not_3_out,
       not_4_out, not_5_out, not_6_out, not_7_out, not_8_out, not_9_out, not_10_out, not_11_out;

  not not_1 (not_1_out, A);
  not not_2 (not_2_out, B);
  not not_3 (not_3_out, C);
  not not_4 (not_4_out, D);
  not not_5 (not_5_out, A);
  not not_6 (not_6_out, B);
  not not_7 (not_7_out, C);
  not not_8 (not_8_out, D);
  not not_9 (not_9_out, A);
  not not_10 (not_10_out, B);
  not not_11 (not_11_out, C);
  nand nand_1 (nand_1_out, not_1_out, not_2_out, D);
  nand nand_2 (hazard_output, nand_1_out, nand_3_out);
  nand nand_3 (nand_3_out, not_3_out, not_4_out);
  nand nand_4 (nand_4_out, not_5_out, not_6_out, D);
  nand nand_5 (nand_5_out, not_7_out, not_8_out);
  nand nand_6 (no_hazard_output, nand_4_out, nand_5_out, nand_7_out);
  nand nand_7 (nand_7_out, not_9_out, not_10_out, not_11_out);
  LED LED1 (.in(hazard_output));
  LED LED1__no_hazard (.in(no_hazard_output));
  _7474_jeden_przerzutnik__nadprogramowo u_7474_jeden_przerzutnik_nadprogramowo_1 (
    .PRE(PRE), .CLR(CLR), .CLK(hazard_output), .D(n7474_jeden_przerzutnik_nadprogramowo_1_q_prime),
    .Q(n7474_jeden_przerzutnik_nadprogramowo_1_q), .Q_prime(n7474_jeden_przerzutnik_nadprogramowo_1_q_prime));
  LED LED2 (.in(n7474_jeden_przerzutnik_nadprogramowo_1_q));
  LED LED2__no_hazard (.in(n7474_jeden_przerzutnik_nadprogramowo_2_q));
  _7474_jeden_przerzutnik__nadprogramowo u_7474_jeden_przerzutnik_nadprogramowo_2 (
    .PRE(PRE_2), .CLR(CLR_2), .CLK(no_hazard_output), .D(n7474_jeden_przerzutnik_nadprogramowo_2_q_prime),
    .Q(n7474_jeden_przerzutnik_nadprogramowo_2_q), .Q_prime(n7474_jeden_przerzutnik_nadprogramowo_2_q_prime));

  // Notes on the sheet:
  //   Funkcja z hazardem
  //   Funkcja bez hazardu
  //   Instrukcja "oscyloskopu" 7474:
  //   1. Należy najpierw ustawić wejścia CLR i PRE na 1, ale nie jednocześnie!
  //   2. Jeśli hazardu nie będzie, LED2 pozostanie w tym stanie, w którym była
  //   3. Jeśli wystąpi hazard statyczny, Logisim się zatrzyma, pokazując, że wystąpiła oscylacja (zaznaczy miejsce gdzie - wyjście Q i układ 7474)
  //   4. W warunkach laboratoryjnych powyższy krok byłby szybkim miganiem LED2, bo układ nie zatrzymałby czasu...
  //   5. Aby zresetować układ należy najpierw ustawić 0 na wejściu CLR lub PRE, a następnie uruchomić symulację (ctrl+e)
  //   6. Błąd o oscylacji powinien zniknąć, teraz należy z powrotem wykonać krok 1. i sprawdzać hazard jak poprzednio
endmodule

module \Porównanie_czasów_trybów_działania__nadprogramowo  (
  input  CLK,
  input  CLR
);

  wire d_ff_1_q, d_ff_1_qn, n7474_jeden_przerzutnik_nadprogramowo_1_q,
       n7474_jeden_przerzutnik_nadprogramowo_1_q_prime, oscyloskop_d_ff_1_q, oscyloskop_d_ff_1_q_prime;

  oscyloskop___D_Flip_Flop oscyloskop_d_ff_1 (
    .CLK(CLK), .D(oscyloskop_d_ff_1_q_prime), .Q(oscyloskop_d_ff_1_q), .Q_prime(oscyloskop_d_ff_1_q_prime));
  D_Flip_Flop d_ff_1 (.clk(CLK), .D(d_ff_1_qn), .Q(d_ff_1_q), .Qn(d_ff_1_qn), .preset(1'b0), .en(1'b1), .reset(1'b0));
  _7474_jeden_przerzutnik__nadprogramowo u_7474_jeden_przerzutnik_nadprogramowo_1 (
    .PRE(1'b1), .CLR(CLR), .CLK(CLK), .D(n7474_jeden_przerzutnik_nadprogramowo_1_q_prime),
    .Q(n7474_jeden_przerzutnik_nadprogramowo_1_q), .Q_prime(n7474_jeden_przerzutnik_nadprogramowo_1_q_prime));
  LED led_1 (.in(oscyloskop_d_ff_1_q));
  LED led_2 (.in(d_ff_1_q));
  LED led_3 (.in(n7474_jeden_przerzutnik_nadprogramowo_1_q));

  // Notes on the sheet:
  //   D Flip-Flop
  //   (5 tick'ów)
  //   ręcznie zbudowany
  //   (4-5 tick'ów)
  //   zbudowany z wbudowanego w logisim
  //   (7 tick'ów - 5 bazowe + 2 na wejście i wyjście)
  //   wbudowany w logisim
endmodule
