// Logisim project z4.circ as structural Verilog: 5 circuits, main circuit D Flip-Flop
module D_Flip_Flop (
  input  PRE,
  input  CLK,
  input  D,
  input  CLR,
  output Q,
  output Q_prime
);

  D_Flip_Flop_part d_ff_1 (.clk(CLK), .D(D), .Q(Q), .Qn(Q_prime), .preset(PRE), .en(1'b1), .reset(CLR));

  // Notes on the sheet:
  //   ENABLE na stałe z wejściem 1
endmodule

// CLK
module \układ_podstawowy  (
  input  X,
  output Q1,
  output Z,
  output Q2
);

  wire and_1_out, and_2_out, and_3_out, CLK_out, d_ff_1_q_prime, or_1_out, or_2_out;

  and and_1 (and_1_out, d_ff_1_q_prime, X);
  and and_2 (and_2_out, X, Q2);
  and and_3 (and_3_out, X, Q1);
  or or_1 (or_1_out, and_1_out, and_2_out);
  or or_2 (or_2_out, and_2_out, and_3_out);
  Clock CLK (.out(CLK_out));
  D_Flip_Flop d_ff_1 (.CLK(CLK_out), .D(or_1_out), .Q(Q1), .Q_prime(d_ff_1_q_prime), .PRE(1'b0), .CLR(1'b0));
  D_Flip_Flop d_ff_2 (.CLK(CLK_out), .D(or_2_out), .Q(Q2), .PRE(1'b0), .CLR(1'b0));  // open: Q_prime
  and and_4 (Z, Q1, Q2);

  // Notes on the sheet:
  //   CLR, PRE
endmodule

module \układ_NAND_NOR  (
  input  X,
  input  X_2,
  output Q1,
  output Q1_2,
  output Z,
  output Z_2,
  output Q2,
  output Q2_2
);

  wire CLK_2_out, CLK_out, d_ff_1_q_prime, d_ff_2_q_prime, d_ff_3_q_prime, nand_1_out, nand_2_out,
       nand_3_out, nand_4_out, nand_5_out, nand_6_out, nand_7_out, nand_8_out, nand_9_out, nand_10_out,
       nand_11_out, nand_12_out;

  nand nand_1 (nand_1_out, d_ff_1_q_prime, X);
  nand nand_2 (nand_2_out, X, Q2);
  nand nand_3 (nand_3_out, X, Q1);
  nand nand_4 (nand_4_out, nand_1_out, nand_2_out);
  nand nand_5 (nand_5_out, nand_2_out, nand_3_out);
  Clock CLK (.out(CLK_out));
  D_Flip_Flop d_ff_1 (.CLK(CLK_out), .D(nand_4_out), .Q(Q1), .Q_prime(d_ff_1_q_prime), .PRE(1'b0), .CLR(1'b0));
  D_Flip_Flop d_ff_2 (.CLK(CLK_out), .D(nand_5_out), .Q(Q2), .Q_prime(d_ff_2_q_prime), .PRE(1'b0), .CLR(1'b0));
  nor nor_1 (Z, d_ff_1_q_prime, d_ff_2_q_prime);
  nand nand_6 (nand_6_out, d_ff_3_q_prime, X_2);
  nand nand_7 (nand_7_out, X_2, Q2_2);
  nand nand_8 (nand_8_out, X_2, Q1_2);
  nand nand_9 (nand_9_out, nand_6_out, nand_7_out);
  nand nand_10 (nand_10_out, nand_7_out, nand_8_out);
  Clock CLK_2 (.out(CLK_2_out));
  D_Flip_Flop d_ff_3 (.CLK(CLK_2_out), .D(nand_9_out), .Q(Q1_2), .Q_prime(d_ff_3_q_prime), .PRE(1'b0), .CLR(1'b0));
  D_Flip_Flop d_ff_4 (.CLK(CLK_2_out), .D(nand_10_out), .Q(Q2_2), .PRE(1'b0), .CLR(1'b0));  // open: Q_prime
  nand nand_11 (nand_11_out, Q1_2, Q2_2);
  nand nand_12 (nand_12_out, Q1_2, Q2_2);
  nand nand_13 (Z_2, nand_11_out, nand_12_out);

  // Notes on the sheet:
  //   Postać 5xNAND,1xNOR
  //   CLR, PRE
  //   Postać 8xNAND
  //   CLR, PRE
endmodule

module JK_Flip_Flop (
  input  PRE,
  input  J,
  input  CLK,
  input  K,
  input  CLR,
  output Q,
  output Q_prime
);

  J_K_Flip_Flop j_k_ff_1 (.J(J), .clk(CLK), .K(K), .Q(Q), .Qn(Q_prime), .preset(PRE), .en(1'b1), .reset(CLR));
endmodule

module \układ_JK  (
  input  X,
  output Q1,
  output Z,
  output Q2
);

  wire and_1_out, CLK_out, jk_ff_2_q_prime, not_1_out;

  Clock CLK (.out(CLK_out));
  not not_1 (not_1_out, X);
  and and_1 (and_1_out, CLK_out, not_1_out);
  JK_Flip_Flop jk_ff_1 (
    .CLK(CLK_out), .Q(Q1), .J(1'b1), .PRE(1'b0), .K(jk_ff_2_q_prime), .CLR(and_1_out));  // open: Q_prime
  JK_Flip_Flop jk_ff_2 (
    .CLK(CLK_out), .Q(Q2), .Q_prime(jk_ff_2_q_prime), .J(Q1), .PRE(1'b0), .K(1'b0), .CLR(and_1_out));
  and and_2 (Z, Q1, Q2);

  // Notes on the sheet:
  //   J1
  //   K2, PRE1, PRE2
endmodule
