// Logisim project z5.circ as structural Verilog: 4 circuits, main circuit D Flip-Flop
module D_Flip_Flop (
  input  PRE,
  input  CLK,
  input  D,
  input  CLR,
  output Q,
  output Q_prime
);

  D_Flip_Flop_part d_ff_1 (.clk(CLK), .D(D), .Q(Q), .Qn(Q_prime), .preset(PRE), .en(1'b1), .reset(CLR));

  // Notes on the sheet:
  //   ENABLE na stałe z wejściem 1
endmodule

// CLK
module \układy  (
  input  X,
  output Z1__Moore,
  output Z2__Moore,
  output Z1__Mealy,
  output Z2__Mealy
);

  wire clock_1_out, d_ff_1_q, d_ff_1_q_prime, d_ff_2_q, d_ff_2_q_prime, jk_ff_1_q, jk_ff_1_q_prime,
       nand_1_out, nand_2_out, nand_3_out, not_1_out, not_2_out;

  nand nand_1 (nand_1_out, d_ff_1_q_prime, X);
  not not_1 (not_1_out, X);
  nand nand_2 (nand_2_out, not_1_out, d_ff_1_q);
  Clock clock_1 (.out(clock_1_out));
  nand nand_3 (nand_3_out, nand_1_out, nand_2_out);
  JK_Flip_Flop jk_ff_1 (
    .CLK(clock_1_out), .Q(jk_ff_1_q), .Q_prime(jk_ff_1_q_prime), .J(X), .PRE(1'b0), .K(X), .CLR(1'b0));
  not not_2 (not_2_out, X);
  D_Flip_Flop d_ff_1 (
    .CLK(clock_1_out), .D(nand_3_out), .Q(d_ff_1_q), .Q_prime(d_ff_1_q_prime), .PRE(1'b0), .CLR(1'b0));
  D_Flip_Flop d_ff_2 (.CLK(clock_1_out), .D(d_ff_1_q), .Q(d_ff_2_q), .Q_prime(d_ff_2_q_prime), .PRE(1'b0), .CLR(1'b0));
  nor nor_1 (Z1__Mealy, not_2_out, jk_ff_1_q_prime);
  nor nor_2 (Z2__Mealy, jk_ff_1_q, not_2_out);
  nor nor_3 (Z1__Moore, d_ff_2_q, d_ff_1_q_prime);
  nor nor_4 (Z2__Moore, d_ff_1_q, d_ff_2_q_prime);
endmodule

module JK_Flip_Flop (
  input  PRE,
  input  J,
  input  CLK,
  input  K,
  input  CLR,
  output Q,
  output Q_prime
);

  J_K_Flip_Flop j_k_ff_1 (.J(J), .clk(CLK), .K(K), .Q(Q), .Qn(Q_prime), .preset(PRE), .en(1'b1), .reset(CLR));
endmodule

module Diagram_czasowy (
);


  // Notes on the sheet:
  //   Z1 Moore
  //   Z2 Moore
  //   Z1 Mealy
  //   Z2 Mealy
  //   Z1 Moore
  //   Z2 Moore
  //   Z1 Mealy
  //   Z2 Mealy
  //   CLK
  //   X
  //   CLK
  //   X
  //   Przejścia (zmiany wartości) Z1,Z2 przesunąłem o jedną kratkę
  //   (pół taktu), aby zaznaczyć rolę opóźnienia w układzie
  //   (wyjścia nie aktualizują się od razu przy zmianie wartości)
endmodule
